# Fritzing sketch Duck Feeder (saved by Fritzing 0.9.3b)
breadboards: 1

parts:
  Part1 = Arduino Uno (Rev3)
  Part3 = Bluetooth HC-05 Macho
  R1 = Resistor [tolerance=±5% resistance=2k package=THT]
  R2 = Resistor [tolerance=±5% resistance=1k package=THT]
  M1 = DC Motor
  S1 = H-Bridge with L298N
  VCC2 = Battery
  VCC3 = Battery block 9V

nets:
  N1: Part1.D9_PWM, S1.IN1
  N2: Part1.D10_PWM/SS, S1.IN2
  GND: Part1.GND, Part3.GND, R1.Pin_1, S1.GND, VCC3.-
  N3: Part1.D0/RX, Part3.TXD
  N4: Part1.D1/TX, R2.Pin_0
  5V: Part1.5V, Part3.VCC, S1.5V
  N5: Part3.RXD, R1.Pin_0, R2.Pin_1
  N6: M1.pin_1, S1.M1-02
  N7: S1.12V, VCC2.+

custom parts:
  H-Bridge with L298N: h-bridge

// code stored in the sketch: Untitled.ino
#include <SoftwareSerial.h>

int led =13;
char state=0;
int motor1= 9;
int motor2= 10;


void setup() {
  pinMode(led,OUTPUT);
  pinMode(motor1,OUTPUT);
  pinMode(motor2, OUTPUT);
  digitalWrite(led, LOW);
  Serial.begin(9600); 

}

void forward()
{
  digitalWrite(motor1,HIGH);
  digitalWrite(motor2,LOW);
  delay(1000);
}
void stopMotor()
{
  digitalWrite(motor1,LOW);
  digitalWrite(motor2,LOW); 
}

void loop() {

  if(Serial.available() > 0)
  {
  
    digitalWrite(led,HIGH);
    state = Serial.read();
    Serial.println(state);

   if(state == '1')
    {
        forward();
        stopMotor();
    }

   else if(state == '0')
    {

      stopMotor();

    }
    
    else
      
      stopMotor();

   }
  
   else 
   stopMotor();

   state = '0';
}
