# Fritzing sketch MasterBluetooth (saved by Fritzing 0.9.3b)
breadboards: 1

parts:
  Part1 = Arduino Uno (Rev3) - ICSP
  Part2 = Bluetooth HC-05 Macho
  VCC1 = 4 x AAA Battery Mount
  S1 = Round Pushbutton
  R1 = Resistor [tolerance=±5% resistance=10k package="0805 [SMD]"]
  R2 = Resistor [tolerance=±5% resistance=2.2k package=THT]
  R3 = Resistor [tolerance=±5% resistance=1k package=THT]

nets:
  N1: Part1.D0/RX, Part2.TXD
  N2: Part1.D1/TX, R3.Pin_1
  5V: Part1.5V, Part2.VCC, S1.leg1
  GND: Part1.GND, Part2.GND, VCC1.-, R1.Pin_0
  N3: Part1.VIN, VCC1.+
  N4: Part2.RXD, R2.Pin_1, R3.Pin_0
  N5: S1.leg0, R1.Pin_1
